// Logisim project CMSC313_Project_Logisim.circ as structural Verilog: 1 circuit, main circuit main
module main (
  input  A,
  input  B,
  input  C,
  input  A1,
  input  B1,
  input  C1
);

  wire and_1_out, and_2_out, and_3_out, and_4_out, and_5_out, nand_1_out, nand_2_out, nand_3_out, nand_4_out,
       nand_5_out, nand_6_out, not_1_out, not_2_out, not_3_out, not_4_out, not_5_out, not_6_out, or_1_out;

  not not_1 (not_1_out, A);
  not not_2 (not_2_out, A1);
  not not_3 (not_3_out, B);
  not not_4 (not_4_out, B1);
  not not_5 (not_5_out, C);
  not not_6 (not_6_out, C1);
  and and_1 (and_1_out, A, B, C);
  and and_2 (and_2_out, not_1_out, B, C);
  and and_3 (and_3_out, A, not_3_out, not_5_out);
  and and_4 (and_4_out, A, not_3_out, C);
  and and_5 (and_5_out, not_1_out, not_3_out, C);
  nand nand_1 (nand_1_out, A1, B1, C1);
  nand nand_2 (nand_2_out, not_2_out, B1, C1);
  nand nand_3 (nand_3_out, A1, not_4_out, not_6_out);
  nand nand_4 (nand_4_out, A1, not_4_out, C1);
  nand nand_5 (nand_5_out, not_2_out, not_4_out, C1);
  or or_1 (or_1_out, and_1_out, and_2_out, and_3_out, and_4_out, and_5_out);
  LED led_1 (.in(or_1_out));
  nand nand_6 (nand_6_out, nand_1_out, nand_2_out, nand_3_out, nand_4_out, nand_5_out);
  LED led_2 (.in(nand_6_out));

  // Notes on the sheet:
  //   AND-OR Circuit:
  //   NAND Circuit:
  //   Project Logisim - CMSC 313 - 10/22/25
  //   f(A,B,C) = ABC+A’BC+AB’C’+AB’C+A’B’C.
  //   f(A,B,C) = ABC+A’BC+AB’C’+AB’C+A’B’C.
endmodule
